// Logisim project arq1_aula05-11.circ as structural Verilog
module ULA (
  input  D,
  input  [3:0] A,
  input  [3:0] B,
  input  [2:0] in_4,
  output Overflow,
  output [3:0] S,
  output Zero
);

  wire add_4_1_overflow, and_1_out, and_2_out, decoder_1_d0, decoder_1_d1, decoder_1_d2, decoder_1_d3,
       decoder_1_d4, decoder_1_d5, decoder_1_d6, decoder_1_d7, not_2_out, sub_4_1_overflow;
  wire [3:0] add_4_1_s, buffer_7_s, not_1_s, or_4bits_1_s, rot_d_1_abcd_2, rot_e_1_abcd_2, sub_4_1_s;

  and and_1 (and_1_out, decoder_1_d2, sub_4_1_overflow);
  or or_1 (Overflow, and_1_out, and_2_out);
  and and_2 (and_2_out, add_4_1_overflow, decoder_1_d1);
  Decoder decoder_1 (
    .E(in_4), .D0(decoder_1_d0), .D1(decoder_1_d1), .D2(decoder_1_d2), .D3(decoder_1_d3), .D4(decoder_1_d4),
    .D5(decoder_1_d5), .D6(decoder_1_d6), .D7(decoder_1_d7));
  add_4 add_4_1 (.in_2(A), .Overflow(add_4_1_overflow), .in_1(B), .S(add_4_1_s));
  // Probe on add_4_1_s
  Buffer buffer_1 (.E(add_4_1_s), .C(decoder_1_d1), .S(S));
  Buffer buffer_2 (.E(B), .C(decoder_1_d0), .S(S));
  sub_4 sub_4_1 (.A(A), .Overflow(sub_4_1_overflow), .B(B), .S(sub_4_1_s));
  // Probe on sub_4_1_s
  Buffer buffer_3 (.E(sub_4_1_s), .C(decoder_1_d2), .S(S));
  nor nor_1 (Zero, S[0], S[1], S[2], S[3], decoder_1_d6, decoder_1_d7);
  NOT not_1 (.E(B), .S(not_1_s));
  OR_4bits or_4bits_1 (.A(A), .B(B), .S(or_4bits_1_s));
  Buffer buffer_4 (.E(or_4bits_1_s), .C(decoder_1_d3), .S(S));
  Buffer buffer_5 (.E(not_1_s), .C(decoder_1_d4), .S(S));
  Rot_E rot_e_1 (.abcd(A), .xy(B[1:0]), .ABCD_2(rot_e_1_abcd_2));
  Rot_D rot_d_1 (.abcd(A), .xy(B[1:0]), .ABCD_2(rot_d_1_abcd_2));
  Buffer buffer_6 (.E(buffer_7_s), .C(decoder_1_d5), .S(S));
  Buffer buffer_7 (.E(rot_e_1_abcd_2), .C(not_2_out), .S(buffer_7_s));
  not not_2 (not_2_out, D);
  Buffer buffer_8 (.E(rot_d_1_abcd_2), .C(D), .S(buffer_7_s));
endmodule

module add_1 (
  input  A,
  input  B,
  input  C,
  output s,
  output vai_1
);

  wire and_1_out, and_2_out, or_1_out, xor_1_out;

  xor xor_1 (xor_1_out, B, C);
  or or_1 (or_1_out, B, C);
  and and_1 (and_1_out, B, C);
  xor xor_2 (s, xor_1_out, A);
  and and_2 (and_2_out, or_1_out, A);
  or or_2 (vai_1, and_2_out, and_1_out);
endmodule

module add_4 (
  input  [3:0] in_1,
  input  [3:0] in_2,
  output Overflow,
  output [3:0] S
);

  wire add_1_2_vai_1, add_1_3_vai_1, add_1_4_vai_1;

  add_1 add_1_1 (.vai_1(Overflow), .A(in_2[3]), .B(in_1[3]), .C(add_1_2_vai_1), .s(S[3]));
  add_1 add_1_2 (.vai_1(add_1_2_vai_1), .A(in_2[2]), .B(in_1[2]), .C(add_1_4_vai_1), .s(S[2]));
  add_1 add_1_3 (.vai_1(add_1_3_vai_1), .A(in_2[0]), .B(in_1[0]), .C(1'b0), .s(S[0]));
  add_1 add_1_4 (.vai_1(add_1_4_vai_1), .A(in_2[1]), .B(in_1[1]), .C(add_1_3_vai_1), .s(S[1]));
endmodule

module sub_4 (
  input  [3:0] B,
  input  [3:0] A,
  output Overflow,
  output [3:0] S
);

  wire sub_1_2_vai_1, sub_1_3_vai_1, sub_1_4_vai_1;

  // Probe on A
  sub_1 sub_1_1 (.vai_1(Overflow), .A(A[3]), .B(B[3]), .C(sub_1_2_vai_1), .s(S[3]));
  sub_1 sub_1_2 (.vai_1(sub_1_2_vai_1), .A(A[2]), .B(B[2]), .C(sub_1_4_vai_1), .s(S[2]));
  // Probe on S
  sub_1 sub_1_3 (.vai_1(sub_1_3_vai_1), .A(A[0]), .B(B[0]), .C(1'b0), .s(S[0]));
  sub_1 sub_1_4 (.vai_1(sub_1_4_vai_1), .A(A[1]), .B(B[1]), .C(sub_1_3_vai_1), .s(S[1]));
  // Probe on B
endmodule

module sub_1 (
  input  A,
  input  B,
  input  C,
  output s,
  output vai_1
);

  wire and_1_out, and_2_out, or_1_out, xor_1_out;

  xor xor_1 (xor_1_out, B, C);
  or or_1 (or_1_out, B, C);
  and and_1 (and_1_out, B, C);
  xor xor_2 (s, xor_1_out, A);
  and and_2 (and_2_out, or_1_out, ~A);  // AND_Gate
  or or_2 (vai_1, and_2_out, and_1_out);
endmodule

module Rot_E (
  input  [3:0] abcd,
  input  [1:0] xy,
  output [3:0] ABCD_2
);

  wire and_1_out, and_2_out, and_3_out, and_4_out, and_5_out, and_6_out, and_7_out, and_8_out, and_9_out;

  and and_1 (and_1_out, abcd[3], ~xy[1], ~xy[0]);  // AND_Gate
  and and_2 (and_2_out, abcd[2], ~xy[1], xy[1]);  // AND_Gate
  and and_3 (and_3_out, abcd[1], xy[1], ~xy[0]);  // AND_Gate
  and and_4 (and_4_out, abcd[0], xy[1], xy[0]);
  and and_5 (and_5_out, abcd[2], ~xy[1], ~xy[0]);  // AND_Gate
  and and_6 (and_6_out, abcd[1], ~xy[1], xy[0]);  // AND_Gate
  and and_7 (and_7_out, abcd[0], xy[1], ~xy[0]);  // AND_Gate
  and and_8 (and_8_out, abcd[1], ~xy[1], ~xy[0]);  // AND_Gate
  and and_9 (and_9_out, abcd[0], ~xy[1], xy[0]);  // AND_Gate
  and and_10 (ABCD_2[0], abcd[0], ~xy[1], ~xy[0]);  // AND_Gate
  or or_1 (ABCD_2[3], and_1_out, and_2_out, and_3_out, and_4_out);
  or or_2 (ABCD_2[2], and_5_out, and_6_out, and_7_out);
  or or_3 (ABCD_2[1], and_8_out, and_9_out);
endmodule

module Rot_D (
  input  [3:0] abcd,
  input  [1:0] xy,
  output [3:0] ABCD_2
);

  wire and_1_out, and_2_out, and_3_out, and_4_out, and_5_out, and_6_out, and_7_out, and_8_out, and_9_out;

  and and_1 (and_1_out, abcd[3], ~xy[1], ~xy[0]);  // AND_Gate
  and and_2 (and_2_out, abcd[2], ~xy[1], xy[1]);  // AND_Gate
  and and_3 (and_3_out, abcd[1], xy[1], ~xy[0]);  // AND_Gate
  and and_4 (and_4_out, abcd[0], xy[1], xy[0]);
  and and_5 (and_5_out, abcd[2], ~xy[1], ~xy[0]);  // AND_Gate
  and and_6 (and_6_out, abcd[1], ~xy[1], xy[0]);  // AND_Gate
  and and_7 (and_7_out, abcd[0], xy[1], ~xy[0]);  // AND_Gate
  and and_8 (and_8_out, abcd[1], ~xy[1], ~xy[0]);  // AND_Gate
  and and_9 (and_9_out, abcd[0], ~xy[1], xy[0]);  // AND_Gate
  and and_10 (ABCD_2[3], abcd[0], ~xy[1], ~xy[0]);  // AND_Gate
  or or_1 (ABCD_2[0], and_1_out, and_2_out, and_3_out, and_4_out);
  or or_2 (ABCD_2[1], and_5_out, and_6_out, and_7_out);
  or or_3 (ABCD_2[2], and_8_out, and_9_out);
endmodule

module Decoder (
  input  [2:0] E,
  output D0,
  output D1,
  output D2,
  output D3,
  output D4,
  output D5,
  output D6,
  output D7
);

  wire not_1_out, not_2_out, not_3_out, not_4_out, not_5_out, not_6_out, not_7_out, not_8_out, not_9_out,
       not_10_out, not_11_out, not_12_out;

  not not_1 (not_1_out, E[0]);
  not not_2 (not_2_out, E[1]);
  not not_3 (not_3_out, E[2]);
  not not_4 (not_4_out, E[0]);
  not not_5 (not_5_out, E[1]);
  not not_6 (not_6_out, E[0]);
  not not_7 (not_7_out, E[2]);
  not not_8 (not_8_out, E[0]);
  not not_9 (not_9_out, E[1]);
  not not_10 (not_10_out, E[2]);
  not not_11 (not_11_out, E[1]);
  not not_12 (not_12_out, E[2]);
  and and_1 (D7, E[0], E[1], E[2]);
  and and_2 (D0, not_1_out, not_2_out, not_3_out);
  and and_3 (D1, not_4_out, not_5_out, E[2]);
  and and_4 (D2, not_6_out, E[1], not_7_out);
  and and_5 (D3, not_8_out, E[1], E[2]);
  and and_6 (D4, E[0], not_9_out, not_10_out);
  and and_7 (D5, E[0], not_11_out, E[2]);
  and and_8 (D6, E[0], E[1], not_12_out);
endmodule

module Buffer (
  input  [3:0] E,
  input  C,
  output [3:0] S
);

  assign S[3] = C ? E[3] : 1'bz;  // Controlled_Buffer controlled_buffer_1
  assign S[1] = C ? E[1] : 1'bz;  // Controlled_Buffer controlled_buffer_2
  assign S[2] = C ? E[2] : 1'bz;  // Controlled_Buffer controlled_buffer_3
  assign S[0] = C ? E[0] : 1'bz;  // Controlled_Buffer controlled_buffer_4
endmodule

module NOT (
  input  [3:0] E,
  output [3:0] S
);

  not not_1 (S[2], E[2]);
  not not_2 (S[3], E[3]);
  not not_3 (S[0], E[0]);
  not not_4 (S[1], E[1]);
endmodule

module OR_4bits (
  input  [3:0] A,
  input  [3:0] B,
  output [3:0] S
);

  // Probe on A
  or or_1 (S[3], A[3], B[3]);
  or or_2 (S[2], A[2], B[2]);
  or or_3 (S[1], A[1], B[1]);
  // Probe on S
  or or_4 (S[0], A[0], B[0]);
  // Probe on B
endmodule

module IR (
  input  Clock,
  input  [7:0] E,
  output [7:0] S
);

  D_Flip_Flop d_ff_1 (.clk(Clock), .D(E[7]), .Q(S[7]));  // open: Qn, preset, en, reset
  D_Flip_Flop d_ff_2 (.clk(Clock), .D(E[6]), .Q(S[6]));  // open: Qn, preset, en, reset
  D_Flip_Flop d_ff_3 (.clk(Clock), .D(E[5]), .Q(S[5]));  // open: Qn, preset, en, reset
  D_Flip_Flop d_ff_4 (.clk(Clock), .D(E[4]), .Q(S[4]));  // open: Qn, preset, en, reset
  D_Flip_Flop d_ff_5 (.clk(Clock), .D(E[3]), .Q(S[3]));  // open: Qn, preset, en, reset
  D_Flip_Flop d_ff_6 (.clk(Clock), .D(E[2]), .Q(S[2]));  // open: Qn, preset, en, reset
  D_Flip_Flop d_ff_7 (.clk(Clock), .D(E[1]), .Q(S[0]));  // open: Qn, preset, en, reset
  D_Flip_Flop d_ff_8 (.clk(Clock), .D(E[0]), .Q(S[1]));  // open: Qn, preset, en, reset
endmodule

module UC (
  input  [7:0] \INSTRUÇÃO ,
  input  Clock,
  input  RESET,
  input  Overflow,
  input  Zero,
  output [3:0] Dados,
  output [3:0] Operando,
  output E,
  output IR,
  output PC,
  output RAM,
  output [2:0] OPCODE,
  output PC_RST,
  output AC,
  output R_1_W_0,
  output Load
);

  wire GOTO_out, JPO_out, JPZ_out;
  wire [1:0] counter_1_q;

  Counter #(.width(2), .max('h3)) counter_1 (.Q(counter_1_q), .clk(Clock), .clr(RESET));  // open: load, D, count, carry
  and JPO (JPO_out, \INSTRUÇÃO [7], \INSTRUÇÃO [6], ~\INSTRUÇÃO [5], \INSTRUÇÃO [4], PC, Overflow);  // AND_Gate
  and and_1 (IR, ~counter_1_q[1], ~counter_1_q[0]);  // AND_Gate
  and and_2 (PC, ~counter_1_q[1], counter_1_q[0]);  // AND_Gate
  and JPZ (JPZ_out, \INSTRUÇÃO [7], \INSTRUÇÃO [6], ~\INSTRUÇÃO [5], ~\INSTRUÇÃO [4], PC, Zero);  // AND_Gate
  or or_1 (Load, JPO_out, JPZ_out, GOTO_out);
  and and_3 (RAM, counter_1_q[1], counter_1_q[0]);
  and and_4 (AC, counter_1_q[1], ~counter_1_q[0]);  // AND_Gate
  and GOTO (GOTO_out, \INSTRUÇÃO [7], \INSTRUÇÃO [6], \INSTRUÇÃO [5], ~\INSTRUÇÃO [4], PC);  // AND_Gate
  nand R_W (R_1_W_0, AC, \INSTRUÇÃO [7], \INSTRUÇÃO [6], \INSTRUÇÃO [5], \INSTRUÇÃO [4]);

  assign Dados = \INSTRUÇÃO [3:0];
  assign E = \INSTRUÇÃO [4];
  assign OPCODE = \INSTRUÇÃO [7:5];
  assign Operando = \INSTRUÇÃO [3:0];
  assign PC_RST = RESET;
endmodule
