// Logisim project arq1_aula06-08.circ as structural Verilog: 2 circuits, main circuit main
module main (
  input  A,
  input  B,
  input  C,
  output Vai_1,
  output S
);

  add_1 add_1_1 (.vai_1(Vai_1), .A(A), .B(B), .C(C), .s(S));
endmodule

module add_1 (
  input  A,
  input  B,
  input  C,
  output s,
  output vai_1
);

  wire and_1_out, and_2_out, or_1_out, xor_1_out;

  xor xor_1 (xor_1_out, B, C);
  or or_1 (or_1_out, B, C);
  and and_1 (and_1_out, B, C);
  xor xor_2 (s, xor_1_out, A);
  and and_2 (and_2_out, or_1_out, A);
  or or_2 (vai_1, and_2_out, and_1_out);
endmodule
