// Logisim project arq1_aula13-08.circ as structural Verilog: 3 circuits, main circuit main
module main (
  input  [3:0] in_1,
  input  [3:0] in_2,
  output out_3,
  output [3:0] out_4
);

  add_4 add_4_1 (.in_2(in_1), .Overflow(out_3), .in_1(in_2), .S(out_4));
endmodule

module add_1 (
  input  A,
  input  B,
  input  C,
  output s,
  output vai_1
);

  wire and_1_out, and_2_out, or_1_out, xor_1_out;

  xor xor_1 (xor_1_out, B, C);
  or or_1 (or_1_out, B, C);
  and and_1 (and_1_out, B, C);
  xor xor_2 (s, xor_1_out, A);
  and and_2 (and_2_out, or_1_out, A);
  or or_2 (vai_1, and_2_out, and_1_out);
endmodule

module add_4 (
  input  [3:0] in_1,
  input  [3:0] in_2,
  output Overflow,
  output [3:0] S
);

  wire add_1_2_vai_1, add_1_3_vai_1, add_1_4_vai_1;

  add_1 add_1_1 (.vai_1(Overflow), .A(in_2[3]), .B(in_1[3]), .C(add_1_2_vai_1), .s(S[3]));
  add_1 add_1_2 (.vai_1(add_1_2_vai_1), .A(in_2[2]), .B(in_1[2]), .C(add_1_4_vai_1), .s(S[2]));
  add_1 add_1_3 (.vai_1(add_1_3_vai_1), .A(in_2[0]), .B(in_1[0]), .C(1'b0), .s(S[0]));
  add_1 add_1_4 (.vai_1(add_1_4_vai_1), .A(in_2[1]), .B(in_1[1]), .C(add_1_3_vai_1), .s(S[1]));
endmodule
