// Logisim project arq1_aula20-08.circ as structural Verilog: 5 circuits, main circuit main
module main (
  input  [3:0] A,
  input  [3:0] B,
  output out_3,
  output out_4,
  output [3:0] S,
  output [3:0] S_2
);

  add_4 add_4_1 (.in_2(A), .Overflow(out_3), .in_1(B), .S(S));
  // Probe on S
  sub_4 sub_4_1 (.A(A), .Overflow(out_4), .B(B), .S(S_2));
  // Probe on S_2
endmodule

module add_1 (
  input  A,
  input  B,
  input  C,
  output s,
  output vai_1
);

  wire and_1_out, and_2_out, or_1_out, xor_1_out;

  xor xor_1 (xor_1_out, B, C);
  or or_1 (or_1_out, B, C);
  and and_1 (and_1_out, B, C);
  xor xor_2 (s, xor_1_out, A);
  and and_2 (and_2_out, or_1_out, A);
  or or_2 (vai_1, and_2_out, and_1_out);
endmodule

module add_4 (
  input  [3:0] in_1,
  input  [3:0] in_2,
  output Overflow,
  output [3:0] S
);

  wire add_1_2_vai_1, add_1_3_vai_1, add_1_4_vai_1;

  add_1 add_1_1 (.vai_1(Overflow), .A(in_2[3]), .B(in_1[3]), .C(add_1_2_vai_1), .s(S[3]));
  add_1 add_1_2 (.vai_1(add_1_2_vai_1), .A(in_2[2]), .B(in_1[2]), .C(add_1_4_vai_1), .s(S[2]));
  add_1 add_1_3 (.vai_1(add_1_3_vai_1), .A(in_2[0]), .B(in_1[0]), .C(1'b0), .s(S[0]));
  add_1 add_1_4 (.vai_1(add_1_4_vai_1), .A(in_2[1]), .B(in_1[1]), .C(add_1_3_vai_1), .s(S[1]));
endmodule

module sub_4 (
  input  [3:0] B,
  input  [3:0] A,
  output Overflow,
  output [3:0] S
);

  wire sub_1_2_vai_1, sub_1_3_vai_1, sub_1_4_vai_1;

  // Probe on A
  sub_1 sub_1_1 (.vai_1(Overflow), .A(A[3]), .B(B[3]), .C(sub_1_2_vai_1), .s(S[3]));
  sub_1 sub_1_2 (.vai_1(sub_1_2_vai_1), .A(A[2]), .B(B[2]), .C(sub_1_4_vai_1), .s(S[2]));
  // Probe on S
  sub_1 sub_1_3 (.vai_1(sub_1_3_vai_1), .A(A[0]), .B(B[0]), .C(1'b0), .s(S[0]));
  sub_1 sub_1_4 (.vai_1(sub_1_4_vai_1), .A(A[1]), .B(B[1]), .C(sub_1_3_vai_1), .s(S[1]));
  // Probe on B
endmodule

module sub_1 (
  input  A,
  input  B,
  input  C,
  output s,
  output vai_1
);

  wire and_1_out, and_2_out, or_1_out, xor_1_out;

  xor xor_1 (xor_1_out, B, C);
  or or_1 (or_1_out, B, C);
  and and_1 (and_1_out, B, C);
  xor xor_2 (s, xor_1_out, A);
  and and_2 (and_2_out, or_1_out, ~A);  // AND_Gate
  or or_2 (vai_1, and_2_out, and_1_out);
endmodule
